# Fritzing sketch SchematicWiiChuck (saved by Fritzing 0.7.4b)
breadboards: 1

parts:
  Arduino_UNO = Arduino
  WiiChuck_Adapter = female pin header, 4 pins [form="♀ (female)"]
  Servo_2 = Basic Servo
  Servo1 = Basic Servo
  Laser = LED - 5mm [color="Red (635nm)" package="5 mm [THT]"]

nets:
  GND: Arduino_UNO.GND, WiiChuck_Adapter.pin4, Servo_2.gnd, Servo1.gnd, Laser.cathode
  N1: Arduino_UNO.D12, Laser.anode
  N2: Arduino_UNO.D10, Servo1.pulse
  N3: Arduino_UNO.D9, Servo_2.pulse
  N4: Arduino_UNO.3V3, WiiChuck_Adapter.pin3
  VCC: Arduino_UNO.+5V, Servo_2.vcc, Servo1.vcc
  N5: Arduino_UNO.A4, WiiChuck_Adapter.pin1
  N6: Arduino_UNO.A5, WiiChuck_Adapter.pin2
